# Fritzing sketch CollectiveComposite (saved by Fritzing 1.0.4)
breadboards: 2

parts:
  M1 = Arduino Nano 33 IOT-smd
  S2 = Pushbutton [package="[SMD]"]
  R1 = Resistor [package="2010 [SMD]"]
  Part1 = Thermal Printer
  U1 = WS2812 RGB LED strip
  M2 = Arduino Nano 33 IOT-smd

nets:
  N1: M1.pin_2, M1.pin_14, M1.pin_19, R1.Pin_1
  N2: M1.pin_13, M1.pin_18
  N3: M1.pin_16, Part1.RXD
  N4: M1.pin_17, Part1.TXD
  N5: M1.pin_24, S2.Pin_3, S2.Pin_4, R1.Pin_0
  N6: S2.Pin_1, S2.Pin_2
  N7: U1.GND, M2.pin_14, M2.pin_19
  N8: U1.VCC, M2.pin_15
  N9: U1.DIN, M2.pin_24
  N10: M2.pin_13, M2.pin_18

notes:
  15V 3000mA DC Power Supply
  5V 3000mA DC Power Supply

custom parts:
  Arduino Nano 33 IOT-smd: The Arduino Nano 33 IoT is the easiest and cheapest point of entry to enhance existing devices (and creating new ones) to be part of the IoT and designing pico-network applications. Whether you are looking at building a sensor network connected to your office or home router, or if you want to create a BLE device sending data to a cellphone, the Nano 33 IoT is your one-stop-solution for many of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
  Resistor: Resistor Basic schematic elements and footprints for 0603, 1206, and PTH resistors.
  WS2812 RGB LED strip: WS2812 strip
